// Logisim project MIPS_CPU.circ as structural Verilog
module IA (
  input  [31:0] instruction,
  input  [1:0] size,
  input  in_3,
  output [4:0] Rs,
  output [4:0] Rt,
  output [4:0] Rd,
  output [4:0] shamt,
  output [5:0] funct,
  output [15:0] immi1,
  output [25:0] immi2
);

  Multiplexer #(.select(2), .width(5), .disabled(0)) multiplexer_1 (
    .in0(instruction[10:6]), .in1(instruction[10:6]), .in2(instruction[20:16]), .in3(instruction[20:16]),
    .out(Rs), .sel(size), .en(in_3));
  Multiplexer #(.select(2), .width(5), .disabled(0)) multiplexer_2 (
    .in0(instruction[15:11]), .in1(instruction[15:11]), .in2(instruction[20:16]), .in3(instruction[20:16]),
    .out(Rt), .sel(size), .en(in_3));
  Multiplexer #(.select(2), .width(5), .disabled(0)) multiplexer_3 (
    .in0(instruction[20:16]), .in1(instruction[20:16]), .in2(instruction[20:16]), .in3(instruction[20:16]),
    .out(Rd), .sel(size), .en(in_3));
  Multiplexer #(.select(2), .width(5), .disabled(0)) multiplexer_4 (
    .in0(instruction[25:21]), .in1(instruction[20:16]), .in2(instruction[20:16]), .in3(instruction[20:16]),
    .out(shamt), .sel(size), .en(in_3));
  Multiplexer #(.select(2), .width(6), .disabled(0)) multiplexer_5 (
    .in0(instruction[31:26]), .in1({6{1'b0}}), .in2({6{1'b0}}), .in3({6{1'b0}}), .out(funct), .sel(size),
    .en(in_3));
  Multiplexer #(.select(2), .width(16), .disabled(0)) multiplexer_6 (
    .in0({16{1'b0}}), .in1(instruction[31:16]), .in2({16{1'b0}}), .in3({16{1'b0}}), .out(immi1), .sel(size),
    .en(in_3));
  Multiplexer #(.select(2), .width(26), .disabled(0)) multiplexer_7 (
    .in0({26{1'b0}}), .in1({26{1'b0}}), .in2(instruction[31:6]), .in3({26{1'b0}}), .out(immi2), .sel(size),
    .en(in_3));
  // also tied to GND on the sheet: {instruction[16], instruction[17], instruction[18], instruction[19], instruction[20]}
endmodule

module DM (
  input  [31:0] in_1,
  input  [23:0] address,
  input  store,
  input  enable,
  input  clock,
  input  clear,
  output [31:0] out_7
);

  RAM #(.addrWidth(24), .dataWidth(32), .bus("separate")) ram_1 (
    .addr(address), .din(in_1), .data(out_7), .str(store), .sel(enable), .clk(clock), .ld(1'b1), .clr(clear));
endmodule

module NPC (
  input  [23:0] offset,
  input  [23:0] PC,
  input  branch,
  input  enable,
  output [23:0] out_5
);

  wire [23:0] multiplexer_1_out;

  Multiplexer #(.width(24)) multiplexer_1 (
    .in0(24'h4), .in1(offset), .out(multiplexer_1_out), .sel(branch), .en(enable));
  Adder #(.width(24)) adder_1 (.a(multiplexer_1_out), .b(PC), .out(out_5));  // open: cin, cout
endmodule

module CO (
  input  [5:0] OP,
  input  [5:0] FUN,
  output [27:0] OP_2,
  output [1:0] SIZE
);

  wire and_3_out, and_5_out, and_8_out, and_9_out, and_10_out, and_11_out, and_15_out, and_16_out,
       and_17_out, and_18_out, and_19_out, and_20_out, and_24_out, and_25_out, and_26_out, and_27_out,
       and_28_out, and_29_out, and_38_out, and_39_out, and_40_out, and_41_out, and_42_out, and_43_out,
       and_50_out, and_52_out;

  // AND_Gate and_1: pin names not known; wires that end beside it: SIZE[0], OP_2[0], OP_2[1], OP_2[2]
  // AND_Gate and_2 has open pins: out=SIZE[1]
  and and_3 (and_3_out, ~OP[0], ~OP[1], ~OP[2], ~OP[3], ~OP[4], ~OP[5]);  // AND_Gate
  and and_4 (OP_2[0], and_3_out, and_5_out);
  and and_5 (and_5_out, ~FUN[0], ~FUN[1], ~FUN[2], ~FUN[3], ~FUN[4], FUN[5]);  // AND_Gate
  and and_6 (OP_2[1], ~OP[0], ~OP[1], ~OP[2], OP[3], ~OP[4], ~OP[5]);  // AND_Gate
  and and_7 (OP_2[2], OP[0], ~OP[1], ~OP[2], OP[3], ~OP[4], ~OP[5]);  // AND_Gate
  and and_8 (and_8_out, ~OP[0], ~OP[1], ~OP[2], ~OP[3], ~OP[4], ~OP[5]);  // AND_Gate
  and and_9 (and_9_out, FUN[0], ~FUN[1], ~FUN[2], ~FUN[3], ~FUN[4], FUN[5]);  // AND_Gate
  and and_10 (and_10_out, ~OP[0], ~OP[1], ~OP[2], ~OP[3], ~OP[4], ~OP[5]);  // AND_Gate
  and and_11 (and_11_out, ~FUN[0], ~FUN[1], FUN[2], ~FUN[3], ~FUN[4], FUN[5]);  // AND_Gate
  and and_12 (OP_2[5], ~OP[0], ~OP[1], OP[2], OP[3], ~OP[4], ~OP[5]);  // AND_Gate
  and and_13 (OP_2[3], and_8_out, and_9_out);
  and and_14 (OP_2[4], and_10_out, and_11_out);
  and and_15 (and_15_out, ~OP[0], ~OP[1], ~OP[2], ~OP[3], ~OP[4], ~OP[5]);  // AND_Gate
  and and_16 (and_16_out, FUN[0], FUN[1], ~FUN[2], ~FUN[3], ~FUN[4], ~FUN[5]);  // AND_Gate
  and and_17 (and_17_out, ~OP[0], ~OP[1], ~OP[2], ~OP[3], ~OP[4], ~OP[5]);  // AND_Gate
  and and_18 (and_18_out, ~FUN[0], FUN[1], ~FUN[2], ~FUN[3], ~FUN[4], ~FUN[5]);  // AND_Gate
  and and_19 (and_19_out, ~OP[0], ~OP[1], ~OP[2], ~OP[3], ~OP[4], ~OP[5]);  // AND_Gate
  and and_20 (and_20_out, ~FUN[0], ~FUN[1], ~FUN[2], ~FUN[3], ~FUN[4], ~FUN[5]);  // AND_Gate
  and and_21 (OP_2[7], and_15_out, and_16_out);
  and and_22 (OP_2[8], and_17_out, and_18_out);
  and and_23 (OP_2[6], and_19_out, and_20_out);
  and and_24 (and_24_out, ~OP[0], ~OP[1], ~OP[2], ~OP[3], ~OP[4], ~OP[5]);  // AND_Gate
  and and_25 (and_25_out, ~FUN[0], FUN[1], ~FUN[2], ~FUN[3], ~FUN[4], FUN[5]);  // AND_Gate
  and and_26 (and_26_out, ~OP[0], ~OP[1], ~OP[2], ~OP[3], ~OP[4], ~OP[5]);  // AND_Gate
  and and_27 (and_27_out, FUN[0], ~FUN[1], FUN[2], ~FUN[3], ~FUN[4], FUN[5]);  // AND_Gate
  and and_28 (and_28_out, ~OP[0], ~OP[1], ~OP[2], ~OP[3], ~OP[4], ~OP[5]);  // AND_Gate
  and and_29 (and_29_out, FUN[0], FUN[1], FUN[2], ~FUN[3], ~FUN[4], FUN[5]);  // AND_Gate
  and and_30 (OP_2[9], and_24_out, and_25_out);
  and and_31 (OP_2[10], and_26_out, and_27_out);
  and and_32 (OP_2[12], and_28_out, and_29_out);
  and and_33 (OP_2[11], OP[0], ~OP[1], OP[2], OP[3], ~OP[4], ~OP[5]);  // AND_Gate
  and and_34 (OP_2[13], OP[0], OP[1], ~OP[2], ~OP[3], ~OP[4], OP[5]);  // AND_Gate
  and and_35 (OP_2[14], OP[0], OP[1], ~OP[2], OP[3], ~OP[4], OP[5]);  // AND_Gate
  and and_36 (OP_2[15], ~OP[0], ~OP[1], OP[2], ~OP[3], ~OP[4], ~OP[5]);  // AND_Gate
  and and_37 (OP_2[16], OP[0], ~OP[1], OP[2], ~OP[3], ~OP[4], ~OP[5]);  // AND_Gate
  and and_38 (and_38_out, ~OP[0], ~OP[1], ~OP[2], ~OP[3], ~OP[4], ~OP[5]);  // AND_Gate
  and and_39 (and_39_out, ~FUN[0], FUN[1], ~FUN[2], FUN[3], ~FUN[4], FUN[5]);  // AND_Gate
  and and_40 (and_40_out, ~OP[0], ~OP[1], ~OP[2], ~OP[3], ~OP[4], ~OP[5]);  // AND_Gate
  and and_41 (and_41_out, FUN[0], FUN[1], ~FUN[2], FUN[3], ~FUN[4], FUN[5]);  // AND_Gate
  and and_42 (and_42_out, ~OP[0], ~OP[1], ~OP[2], ~OP[3], ~OP[4], ~OP[5]);  // AND_Gate
  and and_43 (and_43_out, ~FUN[0], ~FUN[1], ~FUN[2], FUN[3], ~FUN[4], ~FUN[5]);  // AND_Gate
  and and_44 (OP_2[17], and_38_out, and_39_out);
  and and_45 (OP_2[19], and_40_out, and_41_out);
  and and_46 (OP_2[22], and_42_out, and_43_out);
  and and_47 (OP_2[18], OP[0], ~OP[1], OP[2], OP[3], ~OP[4], ~OP[5]);  // AND_Gate
  and and_48 (OP_2[20], ~OP[0], OP[1], ~OP[2], ~OP[3], ~OP[4], ~OP[5]);  // AND_Gate
  and and_49 (OP_2[21], OP[0], OP[1], ~OP[2], ~OP[3], ~OP[4], ~OP[5]);  // AND_Gate
  and and_50 (and_50_out, ~OP[0], ~OP[1], ~OP[2], ~OP[3], ~OP[4], ~OP[5]);  // AND_Gate
  and and_51 (OP_2[23], and_50_out, and_52_out);
  and and_52 (and_52_out, ~FUN[0], ~FUN[1], FUN[2], FUN[3], ~FUN[4], ~FUN[5]);  // AND_Gate
  and and_53 (OP_2[24], ~OP[0], OP[1], OP[2], OP[3], ~OP[4], ~OP[5]);  // AND_Gate
  and and_54 (OP_2[25], OP[0], OP[1], OP[2], OP[3], ~OP[4], ~OP[5]);  // AND_Gate
  and and_55 (OP_2[26], OP[0], ~OP[1], ~OP[2], ~OP[3], ~OP[4], OP[5]);  // AND_Gate
  and and_56 (OP_2[27], OP[0], ~OP[1], ~OP[2], ~OP[3], ~OP[4], ~OP[5]);  // AND_Gate

  // Other names for the same wires on the sheet: Add = OP_2[0]; AddI = OP_2[1]; AddIU = OP_2[2]; AddU = OP_2[3];
  //   And = OP_2[4]; ANDI = OP_2[5]; SLL = OP_2[6]; SRA = OP_2[7]; SRL = OP_2[8]; SUB = OP_2[9]; OR = OP_2[10];
  //   ORI = OP_2[11]; NOR = OP_2[12]; LOADW = OP_2[13]; STOREW = OP_2[14]; BEQ = OP_2[15]; BNE = OP_2[16];
  //   SLT = OP_2[17]; SLTI = OP_2[18]; SLTU = OP_2[19]; JUMP = OP_2[20]; JAL = OP_2[21]; JR = OP_2[22];
  //   SYS = OP_2[23]; XORI = OP_2[24]; LUI = OP_2[25]; LH = OP_2[26]; BLTZ = OP_2[27]

  // Notes on the sheet:
  //   AddI(1000)
  //   AddIU(1001)
  //   Add(100000)
  //   AddU(100001)
  //   And(100100)
  //   ANDI(1100)
  //   SRA(11)
  //   SRL(10)
  //   SLL(0)
  //   SUB(100010)
  //   OR(100101)
  //   NOR(100111)
  //   ORI(1101)
  //   LOADW(100011)
  //   STOREW(101011)
  //   BEQ(100)
  //   BNE(101)
  //   SLT(101010)
  //   SLTU(101011)
  //   JR(1000)
  //   SLTI(1010)
  //   JUMP(10)
  //   JAL(11)
  //   SYS(1100)
  //   XORI(1110)
  //   LUI(1111)
  //   LH(100001)
  //   BLTZ(1)
endmodule
